// Logisim project 245BufferLogic.circ as structural Verilog: 1 circuit, main circuit main
module main (
  input  nRD,
  input  in_2,
  input  in_3,
  input  in_4,
  input  in_5,
  input  in_6,
  input  in_7,
  input  in_8,
  input  in_9,
  input  in_10,
  input  in_11,
  input  in_12,
  input  in_13,
  input  in_14,
  input  in_15,
  input  in_16,
  input  in_17,
  input  nBUSAK,
  input  nIORQ,
  input  nMREQ
);

  wire and_1_out, and_2_out, n74245_1_pin10, n74245_1_pin20;

  and and_1 (and_1_out, nRD, nBUSAK);
  and and_2 (and_2_out, nBUSAK, nIORQ, nMREQ);
  _74245 #(.ShowInternalStructure("true"), .VccGndPorts("true")) u_74245_1 (
    .pin1(and_1_out), .pin2(in_2), .pin3(in_3), .pin4(in_5), .pin5(in_7), .pin6(in_9), .pin7(in_11),
    .pin8(in_13), .pin9(in_15), .pin10(n74245_1_pin10), .pin20(n74245_1_pin20), .pin19(and_2_out),
    .pin18(in_4), .pin17(in_6), .pin16(in_8), .pin15(in_10), .pin14(in_12), .pin13(in_14), .pin12(in_16),
    .pin11(in_17));
  // also tied to GND on the sheet: n74245_1_pin10
  // also tied to VCC on the sheet: n74245_1_pin20

  // Notes on the sheet:
  //   nRD: pull=down
  //   nBUSAK: initial=0x1
  //   nIORQ: initial=0x1
  //   nMREQ: initial=0x1
endmodule
