// Logisim project TestingCPUcardLogic.circ as structural Verilog: 3 circuits, main circuit DataDirLogic
module DataDirLogic (
  input  CPU_Side_IO_Sel,
  input  BDIR_MREQ,
  input  BDIR_RD,
  input  CPU_M1,
  input  CPU_BUSAK
);

  wire and_1_out, and_2_out, nand_1_out, or_1_out;

  and and_1 (and_1_out, CPU_Side_IO_Sel, BDIR_MREQ);
  or or_1 (or_1_out, and_1_out, BDIR_RD);
  nand nand_1 (nand_1_out, BDIR_RD, CPU_M1, CPU_BUSAK);
  and and_2 (and_2_out, or_1_out, nand_1_out);
  LED FromBUS (.in(and_2_out));
  LED #(.active("false")) ToBUS (.in(and_2_out));

  // Notes on the sheet:
  //   CPU_Side_IO_Sel: initial=0x1
  //   BDIR_MREQ: initial=0x1
  //   BDIR_RD: initial=0x1
  //   CPU_M1: initial=0x1
  //   CPU_BUSAK: initial=0x1
endmodule

module OnBoardRamCS (
  input  A15,
  input  BA19,
  input  BA20,
  input  BA21,
  input  MREQ,
  output RAMCS
);

  wire and_1_out, and_2_out, and_3_out, not_1_out;

  not not_1 (not_1_out, A15);
  and and_1 (and_1_out, BA19, not_1_out);
  and and_2 (and_2_out, BA20, not_1_out);
  and and_3 (and_3_out, BA21, not_1_out);
  or or_1 (RAMCS, and_1_out, and_2_out, and_3_out, MREQ);
endmodule

module DataDirLogicZ80 (
  input  SIO,
  input  CTC,
  input  BANK,
  input  INTVEC,
  input  RAM1,
  input  FLASH,
  input  RD,
  input  BUSAK,
  input  IORQ,
  input  M1,
  input  IRQ0,
  input  IRQ1
);

  wire and_1_out, nand_1_out, not_1_out, not_2_out, not_3_out, or_1_out, or_2_out, or_3_out, or_4_out;

  or or_1 (or_1_out, IORQ, M1);
  not not_1 (not_1_out, IRQ0);
  not not_2 (not_2_out, IRQ1);
  nand nand_1 (nand_1_out, SIO, CTC, BANK, INTVEC, RAM1, FLASH);
  not not_3 (not_3_out, RD);
  or or_2 (or_2_out, nand_1_out, RD);
  or or_3 (or_3_out, not_3_out, BUSAK);
  or or_4 (or_4_out, or_1_out, not_1_out, not_2_out);
  and and_1 (and_1_out, or_2_out, or_3_out, or_4_out);
  LED CARD2BUS (.in(and_1_out));
  LED #(.active("false")) BUS2CARD (.in(and_1_out));

  // Notes on the sheet:
  //   SIO: initial=0x1
  //   CTC: initial=0x1
  //   BANK: initial=0x1
  //   INTVEC: initial=0x1
  //   RAM1: initial=0x1
  //   FLASH: initial=0x1
  //   RD: initial=0x1
  //   BUSAK: initial=0x1
  //   IORQ: initial=0x1
  //   M1: initial=0x1
  //   IRQ0: initial=0x1
  //   IRQ1: initial=0x1
  //   On-board devices
  //   Adapted from the Z80 User Manual, page 139, Figure 54
  //   On-board enable
  //   On-board INT
  //   74LS245 DIR:
  //   0 = B to A, 1 = A to B
endmodule
