// Logisim project Glue_Logic.circ as structural Verilog: 2 circuits, main circuit main
module main (
  input  RESET_B,
  input  ROMDIS_B,
  input  RD_B,
  input  MREQ_B,
  input  BA20,
  input  BA19,
  input  A15,
  output RAMSEL_B,
  output ROMSEL_B
);

  wire and_1_out, and_2_out, not_1_out, not_2_out, not_3_out, or_1_out, or_2_out, or_3_out, or_4_out,
       or_5_out, or_6_out;

  nand R (RAMSEL_B, RESET_B, ROMSEL_B);
  nand S (ROMSEL_B, RAMSEL_B, ROMDIS_B);
  not not_1 (not_1_out, BA20);
  not not_2 (not_2_out, BA19);
  not not_3 (not_3_out, A15);
  and and_1 (and_1_out, BA19, not_3_out);
  and and_2 (and_2_out, BA20, not_3_out);
  or or_1 (or_1_out, not_2_out, A15, BA20, MREQ_B);
  or or_2 (or_2_out, not_1_out, A15, BA19, MREQ_B);
  or or_3 (or_3_out, not_1_out, not_2_out, A15, MREQ_B);
  or or_4 (or_4_out, RAMSEL_B, RD_B);
  or or_5 (or_5_out, ROMSEL_B, MREQ_B);
  or or_6 (or_6_out, and_1_out, and_2_out, MREQ_B);
  LED #(.active("false")) ROMCS_B (.in(or_5_out));
  LED #(.active("false")) RAMOE_B (.in(or_4_out));
  LED #(.active("false")) RAMCS1_B (.in(or_6_out));
  LED #(.active("false")) RAMCS2_B (.in(or_1_out));
  LED #(.active("false")) RAMCS3_B (.in(or_2_out));
  LED #(.active("false")) RAMCS4_B (.in(or_3_out));

  // Notes on the sheet:
  //   ROMDIS_B: initial=0x1
  //   RD_B: initial=0x1
  //   MREQ_B: initial=0x1
  //   Pin Nodes
endmodule

module RAMCS (
  input  MREQ,
  input  BA20,
  input  BA19,
  input  A15,
  output RAMCS1,
  output RAMCS2,
  output RAMCS3,
  output RAMCS4
);

  wire and_1_out, and_2_out, not_1_out, not_2_out, not_3_out;

  not not_1 (not_1_out, BA20);
  not not_2 (not_2_out, BA19);
  not not_3 (not_3_out, A15);
  and and_1 (and_1_out, BA19, not_3_out);
  and and_2 (and_2_out, BA20, not_3_out);
  or or_1 (RAMCS2, not_2_out, A15, BA20, MREQ);
  or or_2 (RAMCS3, not_1_out, A15, BA19, MREQ);
  or or_3 (RAMCS4, not_1_out, not_2_out, A15, MREQ);
  or or_4 (RAMCS1, and_1_out, and_2_out, MREQ);
endmodule
